// Logisim project computer.circ as structural Verilog: 11 circuits, main circuit main
module main (
  input  in_1,
  input  in_2,
  input  in_3,
  input  in_4,
  input  in_5,
  input  in_6,
  input  in_7,
  input  in_8,
  input  in_9,
  input  in_10,
  input  in_11,
  input  in_12,
  input  in_13,
  input  in_14,
  input  in_15,
  input  in_16,
  input  in_17,
  input  in_18,
  input  in_19,
  input  in_20,
  input  in_21,
  input  in_22,
  input  in_23,
  input  in_24,
  input  in_25,
  input  in_26,
  input  in_27
);

  wire A_o1, A_o2, A_o3, A_o4, A_o5, A_o6, A_o7, A_o8, A_o9, A_o10, B_o1, B_o2, B_o3, B_o4, B_o5, B_o6, B_o7,
       B_o8, B_o9, B_o10, C_o1, C_o2, C_o3, C_o4, C_o5, C_o6, C_o7, C_o8, C_o9, C_o10, clock_1_out,
       controlledbuffer8_1_o1, controlledbuffer8_1_o2, controlledbuffer8_1_o3, controlledbuffer8_1_o4,
       controlledbuffer8_1_o5, controlledbuffer8_1_o6, controlledbuffer8_1_o7, controlledbuffer8_1_o8,
       controlledbuffer10_2_o1, controlledbuffer10_2_o2, controlledbuffer10_2_o3, controlledbuffer10_2_o4,
       controlledbuffer10_2_o5, controlledbuffer10_2_o6, controlledbuffer10_2_o7, controlledbuffer10_2_o8,
       controlledbuffer10_2_o9, controlledbuffer10_2_o10, controlledbuffer10_3_o1, controlledbuffer10_3_o2,
       controlledbuffer10_3_o3, controlledbuffer10_3_o4, controlledbuffer10_3_o5, controlledbuffer10_3_o6,
       controlledbuffer10_3_o7, controlledbuffer10_3_o8, controlledbuffer10_3_o9, controlledbuffer10_3_o10,
       controlledbuffer10_4_o1, controlledbuffer10_4_o2, controlledbuffer10_4_o3, controlledbuffer10_4_o4,
       controlledbuffer10_4_o5, controlledbuffer10_4_o6, controlledbuffer10_4_o7, controlledbuffer10_4_o8,
       controlledbuffer10_4_o9, controlledbuffer10_4_o10, controlledbuffer10_5_o1, controlledbuffer10_5_o2,
       controlledbuffer10_5_o3, controlledbuffer10_5_o4, controlledbuffer10_5_o5, controlledbuffer10_5_o6,
       controlledbuffer10_5_o7, controlledbuffer10_5_o8, controlledbuffer10_5_o9, controlledbuffer10_5_o10,
       controlledbuffer10_10_o1, controlledbuffer10_10_o2, controlledbuffer10_10_o3,
       controlledbuffer10_10_o4, controlledbuffer10_10_o5, controlledbuffer10_10_o6,
       controlledbuffer10_10_o7, controlledbuffer10_10_o8, controlledbuffer10_10_o9,
       controlledbuffer10_10_o10, D_o1, D_o2, D_o3, D_o4, D_o5, D_o6, D_o7, D_o8, D_o9, D_o10, nandalu_1_o1,
       nandalu_1_o2, nandalu_1_o3, nandalu_1_o4, nandalu_1_o5, nandalu_1_o6, nandalu_1_o7, nandalu_1_o8,
       nandalu_1_o9, nandalu_1_o10;
  wire [7:0] MAR_o1;
  wire [9:0] controlledbuffer10_1_o1, ram_1_dout;

  ControlledBuffer10 controlledbuffer10_1 (
    .A1(in_1), .A2(in_2), .A3(in_3), .A4(in_4), .A5(in_5), .A6(in_6), .A7(in_7), .A8(in_8), .A9(in_9),
    .A10(in_10), .S(in_11), .O1(controlledbuffer10_1_o1[0]), .O2(controlledbuffer10_1_o1[1]),
    .O3(controlledbuffer10_1_o1[2]), .O4(controlledbuffer10_1_o1[3]), .O5(controlledbuffer10_1_o1[4]),
    .O6(controlledbuffer10_1_o1[5]), .O7(controlledbuffer10_1_o1[6]), .O8(controlledbuffer10_1_o1[7]),
    .O9(controlledbuffer10_1_o1[8]), .O10(controlledbuffer10_1_o1[9]));
  Clock clock_1 (.out(clock_1_out));
  ControlledBuffer10 controlledbuffer10_2 (
    .A1(controlledbuffer10_1_o1[0]), .A2(controlledbuffer10_1_o1[1]), .A3(controlledbuffer10_1_o1[2]),
    .A4(controlledbuffer10_1_o1[3]), .A5(controlledbuffer10_1_o1[4]), .A6(controlledbuffer10_1_o1[5]),
    .A7(controlledbuffer10_1_o1[6]), .A8(controlledbuffer10_1_o1[7]), .A9(controlledbuffer10_1_o1[8]),
    .A10(controlledbuffer10_1_o1[9]), .S(in_14), .O1(controlledbuffer10_2_o1), .O2(controlledbuffer10_2_o2),
    .O3(controlledbuffer10_2_o3), .O4(controlledbuffer10_2_o4), .O5(controlledbuffer10_2_o5),
    .O6(controlledbuffer10_2_o6), .O7(controlledbuffer10_2_o7), .O8(controlledbuffer10_2_o8),
    .O9(controlledbuffer10_2_o9), .O10(controlledbuffer10_2_o10));
  ControlledBuffer10 controlledbuffer10_3 (
    .A1(controlledbuffer10_1_o1[0]), .A2(controlledbuffer10_1_o1[1]), .A3(controlledbuffer10_1_o1[2]),
    .A4(controlledbuffer10_1_o1[3]), .A5(controlledbuffer10_1_o1[4]), .A6(controlledbuffer10_1_o1[5]),
    .A7(controlledbuffer10_1_o1[6]), .A8(controlledbuffer10_1_o1[7]), .A9(controlledbuffer10_1_o1[8]),
    .A10(controlledbuffer10_1_o1[9]), .S(in_19), .O1(controlledbuffer10_3_o1), .O2(controlledbuffer10_3_o2),
    .O3(controlledbuffer10_3_o3), .O4(controlledbuffer10_3_o4), .O5(controlledbuffer10_3_o5),
    .O6(controlledbuffer10_3_o6), .O7(controlledbuffer10_3_o7), .O8(controlledbuffer10_3_o8),
    .O9(controlledbuffer10_3_o9), .O10(controlledbuffer10_3_o10));
  ControlledBuffer10 controlledbuffer10_4 (
    .A1(controlledbuffer10_1_o1[0]), .A2(controlledbuffer10_1_o1[1]), .A3(controlledbuffer10_1_o1[2]),
    .A4(controlledbuffer10_1_o1[3]), .A5(controlledbuffer10_1_o1[4]), .A6(controlledbuffer10_1_o1[5]),
    .A7(controlledbuffer10_1_o1[6]), .A8(controlledbuffer10_1_o1[7]), .A9(controlledbuffer10_1_o1[8]),
    .A10(controlledbuffer10_1_o1[9]), .S(in_22), .O1(controlledbuffer10_4_o1), .O2(controlledbuffer10_4_o2),
    .O3(controlledbuffer10_4_o3), .O4(controlledbuffer10_4_o4), .O5(controlledbuffer10_4_o5),
    .O6(controlledbuffer10_4_o6), .O7(controlledbuffer10_4_o7), .O8(controlledbuffer10_4_o8),
    .O9(controlledbuffer10_4_o9), .O10(controlledbuffer10_4_o10));
  ControlledBuffer8 controlledbuffer8_1 (
    .A1(controlledbuffer10_1_o1[0]), .A2(controlledbuffer10_1_o1[1]), .A3(controlledbuffer10_1_o1[2]),
    .A4(controlledbuffer10_1_o1[3]), .A5(controlledbuffer10_1_o1[4]), .A6(controlledbuffer10_1_o1[5]),
    .A7(controlledbuffer10_1_o1[6]), .A8(controlledbuffer10_1_o1[7]), .S(in_25), .O1(controlledbuffer8_1_o1),
    .O2(controlledbuffer8_1_o2), .O3(controlledbuffer8_1_o3), .O4(controlledbuffer8_1_o4),
    .O5(controlledbuffer8_1_o5), .O6(controlledbuffer8_1_o6), .O7(controlledbuffer8_1_o7),
    .O8(controlledbuffer8_1_o8));
  ControlledBuffer10 controlledbuffer10_5 (
    .A1(controlledbuffer10_1_o1[0]), .A2(controlledbuffer10_1_o1[1]), .A3(controlledbuffer10_1_o1[2]),
    .A4(controlledbuffer10_1_o1[3]), .A5(controlledbuffer10_1_o1[4]), .A6(controlledbuffer10_1_o1[5]),
    .A7(controlledbuffer10_1_o1[6]), .A8(controlledbuffer10_1_o1[7]), .A9(controlledbuffer10_1_o1[8]),
    .A10(controlledbuffer10_1_o1[9]), .S(in_27), .O1(controlledbuffer10_5_o1), .O2(controlledbuffer10_5_o2),
    .O3(controlledbuffer10_5_o3), .O4(controlledbuffer10_5_o4), .O5(controlledbuffer10_5_o5),
    .O6(controlledbuffer10_5_o6), .O7(controlledbuffer10_5_o7), .O8(controlledbuffer10_5_o8),
    .O9(controlledbuffer10_5_o9), .O10(controlledbuffer10_5_o10));
  NandRegister10 A (
    .E(clock_1_out), .LOAD(in_12), .A1(controlledbuffer10_2_o1), .A2(controlledbuffer10_2_o2),
    .A3(controlledbuffer10_2_o3), .A4(controlledbuffer10_2_o4), .A5(controlledbuffer10_2_o5),
    .A6(controlledbuffer10_2_o6), .A7(controlledbuffer10_2_o7), .A8(controlledbuffer10_2_o8),
    .A9(controlledbuffer10_2_o9), .A10(controlledbuffer10_2_o10), .O1(A_o1), .O2(A_o2), .O3(A_o3), .O4(A_o4),
    .O5(A_o5), .O6(A_o6), .O7(A_o7), .O8(A_o8), .O9(A_o9), .O10(A_o10));
  NandRegister10 B (
    .E(clock_1_out), .LOAD(in_18), .A1(controlledbuffer10_3_o1), .A2(controlledbuffer10_3_o2),
    .A3(controlledbuffer10_3_o3), .A4(controlledbuffer10_3_o4), .A5(controlledbuffer10_3_o5),
    .A6(controlledbuffer10_3_o6), .A7(controlledbuffer10_3_o7), .A8(controlledbuffer10_3_o8),
    .A9(controlledbuffer10_3_o9), .A10(controlledbuffer10_3_o10), .O1(B_o1), .O2(B_o2), .O3(B_o3), .O4(B_o4),
    .O5(B_o5), .O6(B_o6), .O7(B_o7), .O8(B_o8), .O9(B_o9), .O10(B_o10));
  NandRegister10 D (
    .E(clock_1_out), .LOAD(in_21), .A1(controlledbuffer10_4_o1), .A2(controlledbuffer10_4_o2),
    .A3(controlledbuffer10_4_o3), .A4(controlledbuffer10_4_o4), .A5(controlledbuffer10_4_o5),
    .A6(controlledbuffer10_4_o6), .A7(controlledbuffer10_4_o7), .A8(controlledbuffer10_4_o8),
    .A9(controlledbuffer10_4_o9), .A10(controlledbuffer10_4_o10), .O1(D_o1), .O2(D_o2), .O3(D_o3), .O4(D_o4),
    .O5(D_o5), .O6(D_o6), .O7(D_o7), .O8(D_o8), .O9(D_o9), .O10(D_o10));
  NandRegister8 MAR (
    .E(clock_1_out), .LOAD(in_24), .A1(controlledbuffer8_1_o1), .A2(controlledbuffer8_1_o2),
    .A3(controlledbuffer8_1_o3), .A4(controlledbuffer8_1_o4), .A5(controlledbuffer8_1_o5),
    .A6(controlledbuffer8_1_o6), .A7(controlledbuffer8_1_o7), .A8(controlledbuffer8_1_o8), .O1(MAR_o1[0]),
    .O2(MAR_o1[1]), .O3(MAR_o1[2]), .O4(MAR_o1[3]), .O5(MAR_o1[4]), .O6(MAR_o1[5]), .O7(MAR_o1[6]),
    .O8(MAR_o1[7]));
  NandRegister10 IR (
    .E(clock_1_out), .LOAD(in_26), .A1(controlledbuffer10_5_o1), .A2(controlledbuffer10_5_o2),
    .A3(controlledbuffer10_5_o3), .A4(controlledbuffer10_5_o4), .A5(controlledbuffer10_5_o5),
    .A6(controlledbuffer10_5_o6), .A7(controlledbuffer10_5_o7), .A8(controlledbuffer10_5_o8),
    .A9(controlledbuffer10_5_o9), .A10(controlledbuffer10_5_o10));  // open: O1, O2, O3, O4, O5, O6, O7, O8, O9, O10
  RAM #(.dataWidth(10)) ram_1 (.addr(MAR_o1), .din(controlledbuffer10_1_o1), .dout(ram_1_dout));  // open: we, oe, clk
  ControlledBuffer10 controlledbuffer10_6 (
    .A1(A_o1), .A2(A_o2), .A3(A_o3), .A4(A_o4), .A5(A_o5), .A6(A_o6), .A7(A_o7), .A8(A_o8), .A9(A_o9),
    .A10(A_o10), .S(in_15), .O1(controlledbuffer10_1_o1[0]), .O2(controlledbuffer10_1_o1[1]),
    .O3(controlledbuffer10_1_o1[2]), .O4(controlledbuffer10_1_o1[3]), .O5(controlledbuffer10_1_o1[4]),
    .O6(controlledbuffer10_1_o1[5]), .O7(controlledbuffer10_1_o1[6]), .O8(controlledbuffer10_1_o1[7]),
    .O9(controlledbuffer10_1_o1[8]), .O10(controlledbuffer10_1_o1[9]));
  ControlledBuffer10 controlledbuffer10_7 (
    .A1(B_o1), .A2(B_o2), .A3(B_o3), .A4(B_o4), .A5(B_o5), .A6(B_o6), .A7(B_o7), .A8(B_o8), .A9(B_o9),
    .A10(B_o10), .S(in_20), .O1(controlledbuffer10_1_o1[0]), .O2(controlledbuffer10_1_o1[1]),
    .O3(controlledbuffer10_1_o1[2]), .O4(controlledbuffer10_1_o1[3]), .O5(controlledbuffer10_1_o1[4]),
    .O6(controlledbuffer10_1_o1[5]), .O7(controlledbuffer10_1_o1[6]), .O8(controlledbuffer10_1_o1[7]),
    .O9(controlledbuffer10_1_o1[8]), .O10(controlledbuffer10_1_o1[9]));
  ControlledBuffer10 controlledbuffer10_8 (
    .A1(D_o1), .A2(D_o2), .A3(D_o3), .A4(D_o4), .A5(D_o5), .A6(D_o6), .A7(D_o7), .A8(D_o8), .A9(D_o9),
    .A10(D_o10), .S(in_23), .O1(controlledbuffer10_1_o1[0]), .O2(controlledbuffer10_1_o1[1]),
    .O3(controlledbuffer10_1_o1[2]), .O4(controlledbuffer10_1_o1[3]), .O5(controlledbuffer10_1_o1[4]),
    .O6(controlledbuffer10_1_o1[5]), .O7(controlledbuffer10_1_o1[6]), .O8(controlledbuffer10_1_o1[7]),
    .O9(controlledbuffer10_1_o1[8]), .O10(controlledbuffer10_1_o1[9]));
  ControlledBuffer10 controlledbuffer10_9 (
    .A1(ram_1_dout[0]), .A2(ram_1_dout[1]), .A3(ram_1_dout[2]), .A4(ram_1_dout[3]), .A5(ram_1_dout[4]),
    .A6(ram_1_dout[5]), .A7(ram_1_dout[6]), .A8(ram_1_dout[7]), .A9(ram_1_dout[8]), .A10(ram_1_dout[9]),
    .O1(controlledbuffer10_1_o1[0]), .O2(controlledbuffer10_1_o1[1]), .O3(controlledbuffer10_1_o1[2]),
    .O4(controlledbuffer10_1_o1[3]), .O5(controlledbuffer10_1_o1[4]), .O6(controlledbuffer10_1_o1[5]),
    .O7(controlledbuffer10_1_o1[6]), .O8(controlledbuffer10_1_o1[7]), .O9(controlledbuffer10_1_o1[8]),
    .O10(controlledbuffer10_1_o1[9]));  // open: S
  NandALU nandalu_1 (
    .A9(A_o9), .A10(A_o10), .A1(A_o1), .B1(B_o1), .B2(B_o2), .B3(B_o3), .B4(B_o4), .B5(B_o5), .B6(B_o6),
    .B7(B_o7), .B8(B_o8), .B9(B_o9), .B10(B_o10), .A2(A_o2), .A3(A_o3), .A4(A_o4), .A5(A_o5), .A6(A_o6),
    .A7(A_o7), .A8(A_o8), .O10(nandalu_1_o10), .O2(nandalu_1_o2), .O3(nandalu_1_o3), .O4(nandalu_1_o4),
    .O1(nandalu_1_o1), .O5(nandalu_1_o5), .O6(nandalu_1_o6), .O7(nandalu_1_o7), .O8(nandalu_1_o8),
    .O9(nandalu_1_o9));  // open: AZ, BZ, OC, ABN, AC, BC, C
  ControlledBuffer10 controlledbuffer10_10 (
    .A1(nandalu_1_o1), .A2(nandalu_1_o2), .A3(nandalu_1_o3), .A4(nandalu_1_o4), .A5(nandalu_1_o5),
    .A6(nandalu_1_o6), .A7(nandalu_1_o7), .A8(nandalu_1_o8), .A9(nandalu_1_o9), .A10(nandalu_1_o10),
    .S(in_16), .O1(controlledbuffer10_10_o1), .O2(controlledbuffer10_10_o2), .O3(controlledbuffer10_10_o3),
    .O4(controlledbuffer10_10_o4), .O5(controlledbuffer10_10_o5), .O6(controlledbuffer10_10_o6),
    .O7(controlledbuffer10_10_o7), .O8(controlledbuffer10_10_o8), .O9(controlledbuffer10_10_o9),
    .O10(controlledbuffer10_10_o10));
  NandRegister10 C (
    .E(clock_1_out), .LOAD(in_13), .A1(controlledbuffer10_10_o1), .A2(controlledbuffer10_10_o2),
    .A3(controlledbuffer10_10_o3), .A4(controlledbuffer10_10_o4), .A5(controlledbuffer10_10_o5),
    .A6(controlledbuffer10_10_o6), .A7(controlledbuffer10_10_o7), .A8(controlledbuffer10_10_o8),
    .A9(controlledbuffer10_10_o9), .A10(controlledbuffer10_10_o10), .O1(C_o1), .O2(C_o2), .O3(C_o3),
    .O4(C_o4), .O5(C_o5), .O6(C_o6), .O7(C_o7), .O8(C_o8), .O9(C_o9), .O10(C_o10));
  ControlledBuffer10 controlledbuffer10_11 (
    .A1(C_o1), .A2(C_o2), .A3(C_o3), .A4(C_o4), .A5(C_o5), .A6(C_o6), .A7(C_o7), .A8(C_o8), .A9(C_o9),
    .A10(C_o10), .S(in_17), .O1(controlledbuffer10_1_o1[0]), .O2(controlledbuffer10_1_o1[1]),
    .O3(controlledbuffer10_1_o1[2]), .O4(controlledbuffer10_1_o1[3]), .O5(controlledbuffer10_1_o1[4]),
    .O6(controlledbuffer10_1_o1[5]), .O7(controlledbuffer10_1_o1[6]), .O8(controlledbuffer10_1_o1[7]),
    .O9(controlledbuffer10_1_o1[8]), .O10(controlledbuffer10_1_o1[9]));
endmodule

module NandFullAdder (
  input  A,
  input  B,
  input  Cin,
  output S,
  output Cout
);

  wire nand_1_out, nand_2_out, nand_3_out, nand_4_out, nand_5_out, nand_6_out, nand_7_out, nand_8_out,
       nand_9_out, nand_10_out, nand_11_out;

  nand nand_1 (nand_1_out, B, B);
  nand nand_2 (nand_2_out, A, A);
  nand nand_3 (nand_3_out, A, nand_1_out);
  nand nand_4 (nand_4_out, B, nand_2_out);
  nand nand_5 (nand_5_out, nand_3_out, nand_4_out);
  nand nand_6 (nand_6_out, Cin, Cin);
  nand nand_7 (nand_7_out, nand_5_out, nand_5_out);
  nand nand_8 (nand_8_out, nand_5_out, nand_6_out);
  nand nand_9 (nand_9_out, Cin, nand_7_out);
  nand nand_10 (nand_10_out, Cin, nand_5_out);
  nand nand_11 (nand_11_out, A, B);
  nand nand_12 (S, nand_8_out, nand_9_out);
  nand nand_13 (Cout, nand_10_out, nand_11_out);
endmodule

module NandFullAdder10 (
  input  A1,
  input  B1,
  input  A2,
  input  B2,
  input  A3,
  input  B3,
  input  A4,
  input  B4,
  input  A5,
  input  B5,
  input  A6,
  input  B6,
  input  A7,
  input  B7,
  input  A8,
  input  B8,
  input  A9,
  input  B9,
  input  A10,
  input  B10,
  output S1,
  output S2,
  output S3,
  output S4,
  output S5,
  output S6,
  output S7,
  output S8,
  output S9,
  output S10,
  output C
);

  wire nandfulladder_1_cout, nandfulladder_2_cout, nandfulladder_3_cout, nandfulladder_4_cout,
       nandfulladder_5_cout, nandfulladder_6_cout, nandfulladder_7_cout, nandfulladder_8_cout,
       nandfulladder_9_cout;

  NandFullAdder nandfulladder_1 (.A(A1), .B(B1), .Cin(1'b0), .S(S1), .Cout(nandfulladder_1_cout));
  NandFullAdder nandfulladder_2 (.A(A2), .B(B2), .Cin(nandfulladder_1_cout), .S(S2), .Cout(nandfulladder_2_cout));
  NandFullAdder nandfulladder_3 (.A(A3), .B(B3), .Cin(nandfulladder_2_cout), .S(S3), .Cout(nandfulladder_3_cout));
  NandFullAdder nandfulladder_4 (.A(A4), .B(B4), .Cin(nandfulladder_3_cout), .S(S4), .Cout(nandfulladder_4_cout));
  NandFullAdder nandfulladder_5 (.A(A5), .B(B5), .Cin(nandfulladder_4_cout), .S(S5), .Cout(nandfulladder_5_cout));
  NandFullAdder nandfulladder_6 (.A(A6), .B(B6), .Cin(nandfulladder_5_cout), .S(S6), .Cout(nandfulladder_6_cout));
  NandFullAdder nandfulladder_7 (.A(A7), .B(B7), .Cin(nandfulladder_6_cout), .S(S7), .Cout(nandfulladder_7_cout));
  NandFullAdder nandfulladder_8 (.A(A8), .B(B8), .Cin(nandfulladder_7_cout), .S(S8), .Cout(nandfulladder_8_cout));
  NandFullAdder nandfulladder_9 (.A(A9), .B(B9), .Cin(nandfulladder_8_cout), .S(S9), .Cout(nandfulladder_9_cout));
  NandFullAdder nandfulladder_10 (.A(A10), .B(B10), .Cin(nandfulladder_9_cout), .S(S10), .Cout(C));
endmodule

module NandALU (
  input  A1,
  input  A2,
  input  A3,
  input  A4,
  input  A5,
  input  A6,
  input  A7,
  input  A8,
  input  A9,
  input  A10,
  input  OC,
  input  ABN,
  input  AZ,
  input  AC,
  input  B1,
  input  B2,
  input  B3,
  input  B4,
  input  B5,
  input  B6,
  input  B7,
  input  B8,
  input  B9,
  input  B10,
  input  BZ,
  input  BC,
  output O1,
  output O2,
  output O3,
  output O4,
  output O5,
  output O6,
  output O7,
  output O8,
  output O9,
  output O10,
  output C
);

  wire nand_1_out, nand_2_out, nand_3_out, nand_4_out, nand_5_out, nand_6_out, nand_7_out, nand_8_out,
       nand_9_out, nand_10_out, nand_11_out, nand_12_out, nand_13_out, nand_14_out, nand_15_out, nand_16_out,
       nand_17_out, nand_18_out, nand_19_out, nand_20_out, nand_21_out, nand_22_out, nand_23_out,
       nand_24_out, nand_25_out, nand_26_out, nand_27_out, nand_28_out, nand_29_out, nand_30_out,
       nand_31_out, nand_32_out, nand_33_out, nand_34_out, nand_35_out, nand_36_out, nand_37_out,
       nand_38_out, nand_39_out, nand_40_out, nandfulladder10_1_s1, nandfulladder10_1_s2,
       nandfulladder10_1_s3, nandfulladder10_1_s4, nandfulladder10_1_s5, nandfulladder10_1_s6,
       nandfulladder10_1_s7, nandfulladder10_1_s8, nandfulladder10_1_s9, nandfulladder10_1_s10, nandmux_1_o,
       nandmux_2_o, nandmux_3_o, nandmux_4_o, nandmux_5_o, nandmux_6_o, nandmux_7_o, nandmux_8_o,
       nandmux_9_o, nandmux_10_o, nandmux_11_o, nandmux_12_o, nandmux_13_o, nandmux_14_o, nandmux_15_o,
       nandmux_16_o, nandmux_17_o, nandmux_18_o, nandmux_19_o, nandmux_20_o, nandmux_21_o, nandmux_22_o,
       nandmux_23_o, nandmux_24_o, nandmux_25_o, nandmux_26_o, nandmux_27_o, nandmux_28_o, nandmux_29_o,
       nandmux_30_o, nandmux_31_o, nandmux_32_o, nandmux_33_o, nandmux_34_o, nandmux_35_o, nandmux_36_o,
       nandmux_37_o, nandmux_38_o, nandmux_39_o, nandmux_40_o, nandmux_41_o, nandmux_42_o, nandmux_43_o,
       nandmux_44_o, nandmux_45_o, nandmux_46_o, nandmux_47_o, nandmux_48_o, nandmux_49_o, nandmux_50_o;

  NandMUX nandmux_1 (.A(A1), .S(AZ), .B(1'b0), .O(nandmux_1_o));
  NandMUX nandmux_2 (.A(A2), .S(AZ), .B(1'b0), .O(nandmux_2_o));
  NandMUX nandmux_3 (.A(A3), .S(AZ), .B(1'b0), .O(nandmux_3_o));
  NandMUX nandmux_4 (.A(A4), .S(AZ), .B(1'b0), .O(nandmux_4_o));
  NandMUX nandmux_5 (.A(A5), .S(AZ), .B(1'b0), .O(nandmux_5_o));
  NandMUX nandmux_6 (.A(A6), .S(AZ), .B(1'b0), .O(nandmux_6_o));
  NandMUX nandmux_7 (.A(A7), .S(AZ), .B(1'b0), .O(nandmux_7_o));
  NandMUX nandmux_8 (.A(A8), .S(AZ), .B(1'b0), .O(nandmux_8_o));
  NandMUX nandmux_9 (.A(A9), .S(AZ), .B(1'b0), .O(nandmux_9_o));
  NandMUX nandmux_10 (.A(A10), .S(AZ), .B(1'b0), .O(nandmux_10_o));
  NandMUX nandmux_11 (.A(B1), .S(BZ), .B(1'b0), .O(nandmux_11_o));
  NandMUX nandmux_12 (.A(B2), .S(BZ), .B(1'b0), .O(nandmux_12_o));
  NandMUX nandmux_13 (.A(B3), .S(BZ), .B(1'b0), .O(nandmux_13_o));
  NandMUX nandmux_14 (.A(B4), .S(BZ), .B(1'b0), .O(nandmux_14_o));
  NandMUX nandmux_15 (.A(B5), .S(BZ), .B(1'b0), .O(nandmux_15_o));
  NandMUX nandmux_16 (.A(B6), .S(BZ), .B(1'b0), .O(nandmux_16_o));
  NandMUX nandmux_17 (.A(B7), .S(BZ), .B(1'b0), .O(nandmux_17_o));
  NandMUX nandmux_18 (.A(B8), .S(BZ), .B(1'b0), .O(nandmux_18_o));
  NandMUX nandmux_19 (.A(B9), .S(BZ), .B(1'b0), .O(nandmux_19_o));
  NandMUX nandmux_20 (.A(B10), .S(BZ), .B(1'b0), .O(nandmux_20_o));
  nand nand_1 (nand_1_out, nandmux_1_o, nandmux_1_o);
  nand nand_2 (nand_2_out, nandmux_2_o, nandmux_2_o);
  nand nand_3 (nand_3_out, nandmux_3_o, nandmux_3_o);
  nand nand_4 (nand_4_out, nandmux_4_o, nandmux_4_o);
  nand nand_5 (nand_5_out, nandmux_5_o, nandmux_5_o);
  nand nand_6 (nand_6_out, nandmux_6_o, nandmux_6_o);
  nand nand_7 (nand_7_out, nandmux_7_o, nandmux_7_o);
  nand nand_8 (nand_8_out, nandmux_8_o, nandmux_8_o);
  nand nand_9 (nand_9_out, nandmux_9_o, nandmux_9_o);
  nand nand_10 (nand_10_out, nandmux_10_o, nandmux_10_o);
  nand nand_11 (nand_11_out, nandmux_11_o, nandmux_11_o);
  nand nand_12 (nand_12_out, nandmux_12_o, nandmux_12_o);
  nand nand_13 (nand_13_out, nandmux_13_o, nandmux_13_o);
  nand nand_14 (nand_14_out, nandmux_14_o, nandmux_14_o);
  nand nand_15 (nand_15_out, nandmux_15_o, nandmux_15_o);
  nand nand_16 (nand_16_out, nandmux_16_o, nandmux_16_o);
  nand nand_17 (nand_17_out, nandmux_17_o, nandmux_17_o);
  nand nand_18 (nand_18_out, nandmux_18_o, nandmux_18_o);
  nand nand_19 (nand_19_out, nandmux_19_o, nandmux_19_o);
  nand nand_20 (nand_20_out, nandmux_20_o, nandmux_20_o);
  NandMUX nandmux_21 (.A(nandmux_1_o), .S(AC), .B(nand_1_out), .O(nandmux_21_o));
  NandMUX nandmux_22 (.A(nandmux_2_o), .S(AC), .B(nand_2_out), .O(nandmux_22_o));
  NandMUX nandmux_23 (.A(nandmux_3_o), .S(AC), .B(nand_3_out), .O(nandmux_23_o));
  NandMUX nandmux_24 (.A(nandmux_4_o), .S(AC), .B(nand_4_out), .O(nandmux_24_o));
  NandMUX nandmux_25 (.A(nandmux_5_o), .S(AC), .B(nand_5_out), .O(nandmux_25_o));
  NandMUX nandmux_26 (.A(nandmux_6_o), .S(AC), .B(nand_6_out), .O(nandmux_26_o));
  NandMUX nandmux_27 (.A(nandmux_7_o), .S(AC), .B(nand_7_out), .O(nandmux_27_o));
  NandMUX nandmux_28 (.A(nandmux_8_o), .S(AC), .B(nand_8_out), .O(nandmux_28_o));
  NandMUX nandmux_29 (.A(nandmux_9_o), .S(AC), .B(nand_9_out), .O(nandmux_29_o));
  NandMUX nandmux_30 (.A(nandmux_10_o), .S(AC), .B(nand_10_out), .O(nandmux_30_o));
  NandMUX nandmux_31 (.A(nandmux_11_o), .S(BC), .B(nand_11_out), .O(nandmux_31_o));
  NandMUX nandmux_32 (.A(nandmux_12_o), .S(BC), .B(nand_12_out), .O(nandmux_32_o));
  NandMUX nandmux_33 (.A(nandmux_13_o), .S(BC), .B(nand_13_out), .O(nandmux_33_o));
  NandMUX nandmux_34 (.A(nandmux_14_o), .S(BC), .B(nand_14_out), .O(nandmux_34_o));
  NandMUX nandmux_35 (.A(nandmux_15_o), .S(BC), .B(nand_15_out), .O(nandmux_35_o));
  NandMUX nandmux_36 (.A(nandmux_16_o), .S(BC), .B(nand_16_out), .O(nandmux_36_o));
  NandMUX nandmux_37 (.A(nandmux_17_o), .S(BC), .B(nand_17_out), .O(nandmux_37_o));
  NandMUX nandmux_38 (.A(nandmux_18_o), .S(BC), .B(nand_18_out), .O(nandmux_38_o));
  NandMUX nandmux_39 (.A(nandmux_19_o), .S(BC), .B(nand_19_out), .O(nandmux_39_o));
  NandMUX nandmux_40 (.A(nandmux_20_o), .S(BC), .B(nand_20_out), .O(nandmux_40_o));
  NandFullAdder10 nandfulladder10_1 (
    .B8(nandmux_38_o), .B9(nandmux_39_o), .B10(nandmux_40_o), .B1(nandmux_31_o), .B2(nandmux_32_o),
    .B3(nandmux_33_o), .B4(nandmux_34_o), .B5(nandmux_35_o), .B6(nandmux_36_o), .B7(nandmux_37_o),
    .A9(nandmux_29_o), .A10(nandmux_30_o), .A1(nandmux_21_o), .A2(nandmux_22_o), .A3(nandmux_23_o),
    .A4(nandmux_24_o), .A5(nandmux_25_o), .A6(nandmux_26_o), .A7(nandmux_27_o), .A8(nandmux_28_o),
    .S9(nandfulladder10_1_s9), .S10(nandfulladder10_1_s10), .S1(nandfulladder10_1_s1),
    .S2(nandfulladder10_1_s2), .S3(nandfulladder10_1_s3), .S4(nandfulladder10_1_s4),
    .S5(nandfulladder10_1_s5), .S6(nandfulladder10_1_s6), .S7(nandfulladder10_1_s7),
    .S8(nandfulladder10_1_s8), .C(C));
  nand nand_21 (nand_21_out, nandfulladder10_1_s1, nandfulladder10_1_s1);
  nand nand_22 (nand_22_out, nandfulladder10_1_s2, nandfulladder10_1_s2);
  nand nand_23 (nand_23_out, nandfulladder10_1_s3, nandfulladder10_1_s3);
  nand nand_24 (nand_24_out, nandfulladder10_1_s4, nandfulladder10_1_s4);
  nand nand_25 (nand_25_out, nandfulladder10_1_s5, nandfulladder10_1_s5);
  nand nand_26 (nand_26_out, nandfulladder10_1_s6, nandfulladder10_1_s6);
  nand nand_27 (nand_27_out, nandfulladder10_1_s7, nandfulladder10_1_s7);
  nand nand_28 (nand_28_out, nandfulladder10_1_s8, nandfulladder10_1_s8);
  nand nand_29 (nand_29_out, nandfulladder10_1_s9, nandfulladder10_1_s9);
  nand nand_30 (nand_30_out, nandfulladder10_1_s10, nandfulladder10_1_s10);
  nand nand_31 (nand_31_out, nandmux_21_o, nandmux_31_o);
  nand nand_32 (nand_32_out, nandmux_22_o, nandmux_32_o);
  nand nand_33 (nand_33_out, nandmux_23_o, nandmux_33_o);
  nand nand_34 (nand_34_out, nandmux_24_o, nandmux_34_o);
  nand nand_35 (nand_35_out, nandmux_25_o, nandmux_35_o);
  nand nand_36 (nand_36_out, nandmux_26_o, nandmux_36_o);
  nand nand_37 (nand_37_out, nandmux_27_o, nandmux_37_o);
  nand nand_38 (nand_38_out, nandmux_28_o, nandmux_38_o);
  nand nand_39 (nand_39_out, nandmux_29_o, nandmux_39_o);
  nand nand_40 (nand_40_out, nandmux_30_o, nandmux_40_o);
  NandMUX nandmux_41 (.A(nandfulladder10_1_s1), .S(OC), .B(nand_21_out), .O(nandmux_41_o));
  NandMUX nandmux_42 (.A(nandfulladder10_1_s2), .S(OC), .B(nand_22_out), .O(nandmux_42_o));
  NandMUX nandmux_43 (.A(nandfulladder10_1_s3), .S(OC), .B(nand_23_out), .O(nandmux_43_o));
  NandMUX nandmux_44 (.A(nandfulladder10_1_s4), .S(OC), .B(nand_24_out), .O(nandmux_44_o));
  NandMUX nandmux_45 (.A(nandfulladder10_1_s5), .S(OC), .B(nand_25_out), .O(nandmux_45_o));
  NandMUX nandmux_46 (.A(nandfulladder10_1_s6), .S(OC), .B(nand_26_out), .O(nandmux_46_o));
  NandMUX nandmux_47 (.A(nandfulladder10_1_s7), .S(OC), .B(nand_27_out), .O(nandmux_47_o));
  NandMUX nandmux_48 (.A(nandfulladder10_1_s8), .S(OC), .B(nand_28_out), .O(nandmux_48_o));
  NandMUX nandmux_49 (.A(nandfulladder10_1_s9), .S(OC), .B(nand_29_out), .O(nandmux_49_o));
  NandMUX nandmux_50 (.A(nandfulladder10_1_s10), .S(OC), .B(nand_30_out), .O(nandmux_50_o));
  NandMUX nandmux_51 (.A(nandmux_41_o), .S(ABN), .B(nand_31_out), .O(O1));
  NandMUX nandmux_52 (.A(nandmux_42_o), .S(ABN), .B(nand_32_out), .O(O2));
  NandMUX nandmux_53 (.A(nandmux_43_o), .S(ABN), .B(nand_33_out), .O(O3));
  NandMUX nandmux_54 (.A(nandmux_44_o), .S(ABN), .B(nand_34_out), .O(O4));
  NandMUX nandmux_55 (.A(nandmux_45_o), .S(ABN), .B(nand_35_out), .O(O5));
  NandMUX nandmux_56 (.A(nandmux_46_o), .S(ABN), .B(nand_36_out), .O(O6));
  NandMUX nandmux_57 (.A(nandmux_47_o), .S(ABN), .B(nand_37_out), .O(O7));
  NandMUX nandmux_58 (.A(nandmux_48_o), .S(ABN), .B(nand_38_out), .O(O8));
  NandMUX nandmux_59 (.A(nandmux_49_o), .S(ABN), .B(nand_39_out), .O(O9));
  NandMUX nandmux_60 (.A(nandmux_50_o), .S(ABN), .B(nand_40_out), .O(O10));
endmodule

module NandMUX (
  input  A,
  input  S,
  input  B,
  output O
);

  wire nand_1_out, nand_2_out, nand_3_out;

  nand nand_1 (nand_1_out, S, S);
  nand nand_2 (nand_2_out, A, nand_1_out);
  nand nand_3 (nand_3_out, S, B);
  nand nand_4 (O, nand_2_out, nand_3_out);
endmodule

module NandDFF (
  input  CLK,
  input  A,
  output O,
  output OC
);

  wire nand_1_out, nand_2_out, nand_3_out;

  nand nand_1 (nand_1_out, A, A);
  nand nand_2 (nand_2_out, A, CLK);
  nand nand_3 (nand_3_out, CLK, nand_1_out);
  nand nand_4 (O, nand_2_out, OC);
  nand nand_5 (OC, O, nand_3_out);
endmodule

module NandRegister10 (
  input  E,
  input  LOAD,
  input  A1,
  input  A2,
  input  A3,
  input  A4,
  input  A5,
  input  A6,
  input  A7,
  input  A8,
  input  A9,
  input  A10,
  output O1,
  output O2,
  output O3,
  output O4,
  output O5,
  output O6,
  output O7,
  output O8,
  output O9,
  output O10
);

  wire nand_1_out, nand_2_out, nanddff_1_oc, nanddff_2_oc, nanddff_3_oc, nanddff_4_oc, nanddff_5_oc,
       nanddff_6_oc, nanddff_7_oc, nanddff_8_oc, nanddff_9_oc, nanddff_10_oc;

  nand nand_1 (nand_1_out, E, LOAD);
  nand nand_2 (nand_2_out, nand_1_out, nand_1_out);
  NandDFF nanddff_1 (.CLK(nand_2_out), .A(A1), .O(O1), .OC(nanddff_1_oc));
  NandDFF nanddff_2 (.CLK(nand_2_out), .A(A2), .O(O2), .OC(nanddff_2_oc));
  NandDFF nanddff_3 (.CLK(nand_2_out), .A(A3), .O(O3), .OC(nanddff_3_oc));
  NandDFF nanddff_4 (.CLK(nand_2_out), .A(A4), .O(O4), .OC(nanddff_4_oc));
  NandDFF nanddff_5 (.CLK(nand_2_out), .A(A5), .O(O5), .OC(nanddff_5_oc));
  NandDFF nanddff_6 (.CLK(nand_2_out), .A(A6), .O(O6), .OC(nanddff_6_oc));
  NandDFF nanddff_7 (.CLK(nand_2_out), .A(A7), .O(O7), .OC(nanddff_7_oc));
  NandDFF nanddff_8 (.CLK(nand_2_out), .A(A8), .O(O8), .OC(nanddff_8_oc));
  NandDFF nanddff_9 (.CLK(nand_2_out), .A(A9), .O(O9), .OC(nanddff_9_oc));
  NandDFF nanddff_10 (.CLK(nand_2_out), .A(A10), .O(O10), .OC(nanddff_10_oc));
  // NoConnect on nanddff_1_oc
  // NoConnect on nanddff_2_oc
  // NoConnect on nanddff_3_oc
  // NoConnect on nanddff_4_oc
  // NoConnect on nanddff_5_oc
  // NoConnect on nanddff_6_oc
  // NoConnect on nanddff_7_oc
  // NoConnect on nanddff_8_oc
  // NoConnect on nanddff_9_oc
  // NoConnect on nanddff_10_oc
endmodule

module NandMUX10 (
  input  A1,
  input  B1,
  input  A2,
  input  B2,
  input  A3,
  input  B3,
  input  A4,
  input  B4,
  input  A5,
  input  B5,
  input  A6,
  input  B6,
  input  A7,
  input  B7,
  input  A8,
  input  B8,
  input  A9,
  input  B9,
  input  A10,
  input  B10,
  input  S,
  output O1,
  output O2,
  output O3,
  output O4,
  output O5,
  output O6,
  output O7,
  output O8,
  output O9,
  output O10
);

  NandMUX nandmux_1 (.A(A1), .S(S), .B(B1), .O(O1));
  NandMUX nandmux_2 (.A(A2), .S(S), .B(B2), .O(O2));
  NandMUX nandmux_3 (.A(A3), .S(S), .B(B3), .O(O3));
  NandMUX nandmux_4 (.A(A4), .S(S), .B(B4), .O(O4));
  NandMUX nandmux_5 (.A(A5), .S(S), .B(B5), .O(O5));
  NandMUX nandmux_6 (.A(A6), .S(S), .B(B6), .O(O6));
  NandMUX nandmux_7 (.A(A7), .S(S), .B(B7), .O(O7));
  NandMUX nandmux_8 (.A(A8), .S(S), .B(B8), .O(O8));
  NandMUX nandmux_9 (.A(A9), .S(S), .B(B9), .O(O9));
  NandMUX nandmux_10 (.A(A10), .S(S), .B(B10), .O(O10));
endmodule

module ControlledBuffer10 (
  input  A1,
  input  A2,
  input  A3,
  input  A4,
  input  A5,
  input  A6,
  input  A7,
  input  A8,
  input  A9,
  input  A10,
  input  S,
  output O1,
  output O2,
  output O3,
  output O4,
  output O5,
  output O6,
  output O7,
  output O8,
  output O9,
  output O10
);

  assign O1 = S ? A1 : 1'bz;  // Controlled_Buffer controlled_buffer_1
  assign O2 = S ? A2 : 1'bz;  // Controlled_Buffer controlled_buffer_2
  assign O3 = S ? A3 : 1'bz;  // Controlled_Buffer controlled_buffer_3
  assign O4 = S ? A4 : 1'bz;  // Controlled_Buffer controlled_buffer_4
  assign O5 = S ? A5 : 1'bz;  // Controlled_Buffer controlled_buffer_5
  assign O6 = S ? A6 : 1'bz;  // Controlled_Buffer controlled_buffer_6
  assign O7 = S ? A7 : 1'bz;  // Controlled_Buffer controlled_buffer_7
  assign O8 = S ? A8 : 1'bz;  // Controlled_Buffer controlled_buffer_8
  assign O9 = S ? A9 : 1'bz;  // Controlled_Buffer controlled_buffer_9
  assign O10 = S ? A10 : 1'bz;  // Controlled_Buffer controlled_buffer_10
endmodule

module NandRegister8 (
  input  E,
  input  LOAD,
  input  A1,
  input  A2,
  input  A3,
  input  A4,
  input  A5,
  input  A6,
  input  A7,
  input  A8,
  output O1,
  output O2,
  output O3,
  output O4,
  output O5,
  output O6,
  output O7,
  output O8
);

  wire nand_1_out, nand_2_out, nanddff_1_oc, nanddff_2_oc, nanddff_3_oc, nanddff_4_oc, nanddff_5_oc,
       nanddff_6_oc, nanddff_7_oc, nanddff_8_oc;

  nand nand_1 (nand_1_out, E, LOAD);
  nand nand_2 (nand_2_out, nand_1_out, nand_1_out);
  NandDFF nanddff_1 (.CLK(nand_2_out), .A(A1), .O(O1), .OC(nanddff_1_oc));
  NandDFF nanddff_2 (.CLK(nand_2_out), .A(A2), .O(O2), .OC(nanddff_2_oc));
  NandDFF nanddff_3 (.CLK(nand_2_out), .A(A3), .O(O3), .OC(nanddff_3_oc));
  NandDFF nanddff_4 (.CLK(nand_2_out), .A(A4), .O(O4), .OC(nanddff_4_oc));
  NandDFF nanddff_5 (.CLK(nand_2_out), .A(A5), .O(O5), .OC(nanddff_5_oc));
  NandDFF nanddff_6 (.CLK(nand_2_out), .A(A6), .O(O6), .OC(nanddff_6_oc));
  NandDFF nanddff_7 (.CLK(nand_2_out), .A(A7), .O(O7), .OC(nanddff_7_oc));
  NandDFF nanddff_8 (.CLK(nand_2_out), .A(A8), .O(O8), .OC(nanddff_8_oc));
  // NoConnect on nanddff_1_oc
  // NoConnect on nanddff_2_oc
  // NoConnect on nanddff_3_oc
  // NoConnect on nanddff_4_oc
  // NoConnect on nanddff_5_oc
  // NoConnect on nanddff_6_oc
  // NoConnect on nanddff_7_oc
  // NoConnect on nanddff_8_oc
endmodule

module ControlledBuffer8 (
  input  A1,
  input  A2,
  input  A3,
  input  A4,
  input  A5,
  input  A6,
  input  A7,
  input  A8,
  input  S,
  output O1,
  output O2,
  output O3,
  output O4,
  output O5,
  output O6,
  output O7,
  output O8
);

  assign O1 = S ? A1 : 1'bz;  // Controlled_Buffer controlled_buffer_1
  assign O2 = S ? A2 : 1'bz;  // Controlled_Buffer controlled_buffer_2
  assign O3 = S ? A3 : 1'bz;  // Controlled_Buffer controlled_buffer_3
  assign O4 = S ? A4 : 1'bz;  // Controlled_Buffer controlled_buffer_4
  assign O5 = S ? A5 : 1'bz;  // Controlled_Buffer controlled_buffer_5
  assign O6 = S ? A6 : 1'bz;  // Controlled_Buffer controlled_buffer_6
  assign O7 = S ? A7 : 1'bz;  // Controlled_Buffer controlled_buffer_7
  assign O8 = S ? A8 : 1'bz;  // Controlled_Buffer controlled_buffer_8
endmodule
