// Logisim project sutra_1.circ as structural Verilog: 21 circuits, main circuit main
module main (
);

  wire [2:0] buffer10_1_o_2;
  wire [6:0] aluflagsregister_1_o, buffer10_1_o;
  wire [9:0] A_o, alu_1_o, ALU_RESULT_o, B_o, buffer10_4_o, C_o, D_o, ram_1_data;
  wire [19:0] mux2to1_20_1_o, normalregister20_1_o, synccounter_1_o;

  NormalRegister B (.I({buffer10_1_o_2, buffer10_1_o}), .O(B_o));  // open: CLK, LL, LH, SB
  Buffer10 buffer10_1 (.I(B_o), .O({buffer10_1_o_2, buffer10_1_o}));  // open: E
  UniversalShiftRegister A (.I({buffer10_1_o_2, buffer10_1_o}), .O(A_o));  // open: CLK, LL, LH, SB, S1, S2
  Buffer10 buffer10_2 (.I(A_o), .O({buffer10_1_o_2, buffer10_1_o}));  // open: E
  NormalRegister C (.I({buffer10_1_o_2, buffer10_1_o}), .O(C_o));  // open: CLK, LL, LH, SB
  Buffer10 buffer10_3 (.I(C_o), .O({buffer10_1_o_2, buffer10_1_o}));  // open: E
  Buffer10 buffer10_4 (.I({buffer10_1_o_2, buffer10_1_o}), .O(buffer10_4_o));  // open: E
  ALUFlagsRegister aluflagsregister_1 (.I(buffer10_1_o), .O(aluflagsregister_1_o));  // open: CLK, LL, LH, SB
  NormalRegister20 normalregister20_1 (.O(normalregister20_1_o));  // open: CLK, LL, LH, SB, I
  SyncCounter synccounter_1 (.O(synccounter_1_o));  // open: SB, CLK, L, I
  ALU alu_1 (
    .A(A_o), .B(buffer10_4_o), .AZ(aluflagsregister_1_o[0]), .AC(aluflagsregister_1_o[1]),
    .BZ(aluflagsregister_1_o[2]), .BC(aluflagsregister_1_o[3]), .Cin(aluflagsregister_1_o[4]),
    .N(aluflagsregister_1_o[5]), .OC(aluflagsregister_1_o[6]), .O(alu_1_o));  // open: Cout
  NormalRegister D (.I({buffer10_1_o_2, buffer10_1_o}), .O(D_o));  // open: CLK, LL, LH, SB
  RAM #(.addrWidth(20), .dataWidth(10), .databus("bidir"), .\type ("nonvolatile")) ram_1 (
    .addr(mux2to1_20_1_o), .data(ram_1_data));  // open: we, oe, clk
  Mux2To1_20 mux2to1_20_1 (.A(normalregister20_1_o), .B(synccounter_1_o), .O(mux2to1_20_1_o));  // open: S
  NormalRegister ALU_RESULT (.I(alu_1_o), .O(ALU_RESULT_o));  // open: CLK, LL, LH, SB
  Buffer10 buffer10_5 (.I(D_o), .O({buffer10_1_o_2, buffer10_1_o}));  // open: E
  Buffer10 buffer10_6 (.I(ALU_RESULT_o), .O({buffer10_1_o_2, buffer10_1_o}));  // open: E
  Buffer10 buffer10_7 (.I(ram_1_data), .O({buffer10_1_o_2, buffer10_1_o}));  // open: E
endmodule

module SRLatch (
  input  S,
  input  R,
  input  SB,
  output O,
  output OC
);

  wire nand_1_out, nand_2_out;

  nand nand_1 (nand_1_out, S, S);
  nand nand_2 (nand_2_out, R, R);
  nand nand_3 (O, nand_1_out, SB, OC);
  nand nand_4 (OC, O, nand_2_out);
endmodule

module DLatch (
  input  E,
  input  D,
  input  SB,
  output O,
  output OC
);

  wire nand_1_out, nand_2_out;

  nand nand_1 (nand_1_out, E, D);
  nand nand_2 (nand_2_out, nand_1_out, E);
  nand nand_3 (O, nand_1_out, SB, OC);
  nand nand_4 (OC, O, nand_2_out);
endmodule

module UniversalShiftRegister (
  input  CLK,
  input  LL,
  input  LH,
  input  SB,
  input  S1,
  input  S2,
  input  [9:0] I,
  output [9:0] O
);

  wire mux4to1_1_o, mux4to1_2_o, mux4to1_3_o, mux4to1_4_o, mux4to1_5_o, mux4to1_6_o, mux4to1_7_o,
       mux4to1_8_o, mux4to1_9_o, mux4to1_10_o, nand_1_out, nand_2_out, nand_3_out, nand_4_out;

  nand nand_1 (nand_1_out, CLK, LL);
  nand nand_2 (nand_2_out, nand_1_out, nand_1_out);
  nand nand_3 (nand_3_out, CLK, LH);
  nand nand_4 (nand_4_out, nand_3_out, nand_3_out);
  Mux4To1 mux4to1_1 (.A(O[1]), .B(1'b0), .C(I[0]), .D(1'b0), .S1(S1), .S2(S2), .O(mux4to1_1_o));
  DFlipFlop dflipflop_1 (.CLK(nand_2_out), .D(mux4to1_1_o), .SB(SB), .O(O[0]));  // open: OC
  Mux4To1 mux4to1_2 (.A(O[2]), .B(O[0]), .C(I[1]), .D(1'b0), .S1(S1), .S2(S2), .O(mux4to1_2_o));
  DFlipFlop dflipflop_2 (.CLK(nand_2_out), .D(mux4to1_2_o), .SB(SB), .O(O[1]));  // open: OC
  Mux4To1 mux4to1_3 (.A(O[3]), .B(O[1]), .C(I[2]), .D(1'b0), .S1(S1), .S2(S2), .O(mux4to1_3_o));
  DFlipFlop dflipflop_3 (.CLK(nand_2_out), .D(mux4to1_3_o), .SB(SB), .O(O[2]));  // open: OC
  Mux4To1 mux4to1_4 (.A(O[4]), .B(O[2]), .C(I[3]), .D(1'b0), .S1(S1), .S2(S2), .O(mux4to1_4_o));
  DFlipFlop dflipflop_4 (.CLK(nand_2_out), .D(mux4to1_4_o), .SB(SB), .O(O[3]));  // open: OC
  Mux4To1 mux4to1_5 (.A(O[5]), .B(O[3]), .C(I[4]), .D(1'b0), .S1(S1), .S2(S2), .O(mux4to1_5_o));
  DFlipFlop dflipflop_5 (.CLK(nand_2_out), .D(mux4to1_5_o), .SB(SB), .O(O[4]));  // open: OC
  Mux4To1 mux4to1_6 (.A(O[6]), .B(O[4]), .C(I[5]), .D(1'b0), .S1(S1), .S2(S2), .O(mux4to1_6_o));
  DFlipFlop dflipflop_6 (.CLK(nand_4_out), .D(mux4to1_6_o), .SB(SB), .O(O[5]));  // open: OC
  Mux4To1 mux4to1_7 (.A(O[7]), .B(O[5]), .C(I[6]), .D(1'b0), .S1(S1), .S2(S2), .O(mux4to1_7_o));
  DFlipFlop dflipflop_7 (.CLK(nand_4_out), .D(mux4to1_7_o), .SB(SB), .O(O[6]));  // open: OC
  Mux4To1 mux4to1_8 (.A(O[8]), .B(O[6]), .C(I[7]), .D(1'b0), .S1(S1), .S2(S2), .O(mux4to1_8_o));
  DFlipFlop dflipflop_8 (.CLK(nand_4_out), .D(mux4to1_8_o), .SB(SB), .O(O[7]));  // open: OC
  Mux4To1 mux4to1_9 (.A(O[9]), .B(O[7]), .C(I[8]), .D(1'b0), .S1(S1), .S2(S2), .O(mux4to1_9_o));
  DFlipFlop dflipflop_9 (.CLK(nand_4_out), .D(mux4to1_9_o), .SB(SB), .O(O[8]));  // open: OC
  Mux4To1 mux4to1_10 (.A(1'b0), .B(O[8]), .C(I[9]), .D(1'b0), .S1(S1), .S2(S2), .O(mux4to1_10_o));
  DFlipFlop dflipflop_10 (.CLK(nand_4_out), .D(mux4to1_10_o), .SB(SB), .O(O[9]));  // open: OC
endmodule

module Mux2To1 (
  input  A,
  input  B,
  input  S,
  output O
);

  wire nand_1_out, nand_2_out, nand_3_out;

  nand nand_1 (nand_1_out, S, S);
  nand nand_2 (nand_2_out, A, nand_1_out);
  nand nand_3 (nand_3_out, B, S);
  nand nand_4 (O, nand_2_out, nand_3_out);
endmodule

module Mux4To1 (
  input  A,
  input  B,
  input  C,
  input  D,
  input  S1,
  input  S2,
  output O
);

  wire mux2to1_1_o, mux2to1_2_o;

  Mux2To1 mux2to1_1 (.A(A), .B(C), .S(S1), .O(mux2to1_1_o));
  Mux2To1 mux2to1_2 (.A(B), .B(D), .S(S1), .O(mux2to1_2_o));
  Mux2To1 mux2to1_3 (.A(mux2to1_1_o), .B(mux2to1_2_o), .S(S2), .O(O));
endmodule

module DFlipFlop (
  input  CLK,
  input  D,
  input  SB,
  output O,
  output OC
);

  wire dlatch_1_o, nand_1_out;

  DLatch dlatch_1 (.E(CLK), .D(D), .SB(SB), .O(dlatch_1_o));  // open: OC
  nand nand_1 (nand_1_out, CLK, CLK);
  DLatch dlatch_2 (.E(nand_1_out), .D(dlatch_1_o), .SB(SB), .O(O), .OC(OC));
endmodule

module NormalRegister (
  input  CLK,
  input  LL,
  input  LH,
  input  SB,
  input  [9:0] I,
  output [9:0] O
);

  wire nand_1_out, nand_2_out, nand_3_out, nand_4_out;

  nand nand_1 (nand_1_out, CLK, LL);
  nand nand_2 (nand_2_out, nand_1_out, nand_1_out);
  nand nand_3 (nand_3_out, CLK, LH);
  nand nand_4 (nand_4_out, nand_3_out, nand_3_out);
  DLatch dlatch_1 (.E(nand_2_out), .D(I[0]), .SB(SB), .O(O[0]));  // open: OC
  DLatch dlatch_2 (.E(nand_2_out), .D(I[1]), .SB(SB), .O(O[1]));  // open: OC
  DLatch dlatch_3 (.E(nand_2_out), .D(I[2]), .SB(SB), .O(O[2]));  // open: OC
  DLatch dlatch_4 (.E(nand_2_out), .D(I[3]), .SB(SB), .O(O[3]));  // open: OC
  DLatch dlatch_5 (.E(nand_2_out), .D(I[4]), .SB(SB), .O(O[4]));  // open: OC
  DLatch dlatch_6 (.E(nand_4_out), .D(I[5]), .SB(SB), .O(O[5]));  // open: OC
  DLatch dlatch_7 (.E(nand_4_out), .D(I[6]), .SB(SB), .O(O[6]));  // open: OC
  DLatch dlatch_8 (.E(nand_4_out), .D(I[7]), .SB(SB), .O(O[7]));  // open: OC
  DLatch dlatch_9 (.E(nand_4_out), .D(I[8]), .SB(SB), .O(O[8]));  // open: OC
  DLatch dlatch_10 (.E(nand_4_out), .D(I[9]), .SB(SB), .O(O[9]));  // open: OC
endmodule

module NormalRegister20 (
  input  CLK,
  input  LL,
  input  LH,
  input  SB,
  input  [19:0] I,
  output [19:0] O
);

  wire nand_1_out, nand_2_out, nand_3_out, nand_4_out;

  nand nand_1 (nand_1_out, CLK, LL);
  nand nand_2 (nand_2_out, nand_1_out, nand_1_out);
  nand nand_3 (nand_3_out, CLK, LH);
  nand nand_4 (nand_4_out, nand_3_out, nand_3_out);
  DLatch dlatch_1 (.E(nand_2_out), .D(I[0]), .SB(SB), .O(O[0]));  // open: OC
  DLatch dlatch_2 (.E(nand_2_out), .D(I[1]), .SB(SB), .O(O[1]));  // open: OC
  DLatch dlatch_3 (.E(nand_2_out), .D(I[2]), .SB(SB), .O(O[2]));  // open: OC
  DLatch dlatch_4 (.E(nand_2_out), .D(I[3]), .SB(SB), .O(O[3]));  // open: OC
  DLatch dlatch_5 (.E(nand_2_out), .D(I[4]), .SB(SB), .O(O[4]));  // open: OC
  DLatch dlatch_6 (.E(nand_2_out), .D(I[5]), .SB(SB), .O(O[5]));  // open: OC
  DLatch dlatch_7 (.E(nand_2_out), .D(I[6]), .SB(SB), .O(O[6]));  // open: OC
  DLatch dlatch_8 (.E(nand_2_out), .D(I[7]), .SB(SB), .O(O[7]));  // open: OC
  DLatch dlatch_9 (.E(nand_2_out), .D(I[8]), .SB(SB), .O(O[8]));  // open: OC
  DLatch dlatch_10 (.E(nand_2_out), .D(I[9]), .SB(SB), .O(O[9]));  // open: OC
  DLatch dlatch_11 (.E(nand_4_out), .D(I[10]), .SB(SB), .O(O[10]));  // open: OC
  DLatch dlatch_12 (.E(nand_4_out), .D(I[11]), .SB(SB), .O(O[11]));  // open: OC
  DLatch dlatch_13 (.E(nand_4_out), .D(I[12]), .SB(SB), .O(O[12]));  // open: OC
  DLatch dlatch_14 (.E(nand_4_out), .D(I[13]), .SB(SB), .O(O[13]));  // open: OC
  DLatch dlatch_15 (.E(nand_4_out), .D(I[14]), .SB(SB), .O(O[14]));  // open: OC
  DLatch dlatch_16 (.E(nand_4_out), .D(I[15]), .SB(SB), .O(O[15]));  // open: OC
  DLatch dlatch_17 (.E(nand_4_out), .D(I[16]), .SB(SB), .O(O[16]));  // open: OC
  DLatch dlatch_18 (.E(nand_4_out), .D(I[17]), .SB(SB), .O(O[17]));  // open: OC
  DLatch dlatch_19 (.E(nand_4_out), .D(I[18]), .SB(SB), .O(O[18]));  // open: OC
  DLatch dlatch_20 (.E(nand_4_out), .D(I[19]), .SB(SB), .O(O[19]));  // open: OC
endmodule

module SyncCounter (
  input  SB,
  input  CLK,
  input  L,
  input  [19:0] I,
  output [19:0] O
);

  wire jkflipflop_12_o, mux2to1_1_o, mux2to1_2_o, mux2to1_3_o, mux2to1_4_o, mux2to1_5_o, mux2to1_6_o,
       mux2to1_7_o, mux2to1_8_o, mux2to1_9_o, mux2to1_10_o, mux2to1_11_o, mux2to1_12_o, mux2to1_13_o,
       mux2to1_14_o, mux2to1_15_o, mux2to1_16_o, mux2to1_17_o, mux2to1_18_o, mux2to1_19_o, mux2to1_20_o,
       mux2to1_21_o, mux2to1_22_o, mux2to1_23_o, mux2to1_24_o, mux2to1_25_o, mux2to1_26_o, mux2to1_27_o,
       mux2to1_28_o, mux2to1_29_o, mux2to1_30_o, mux2to1_31_o, mux2to1_32_o, mux2to1_33_o, mux2to1_34_o,
       mux2to1_35_o, mux2to1_36_o, mux2to1_37_o, mux2to1_38_o, mux2to1_39_o, mux2to1_40_o, nand_1_out,
       nand_2_out, nand_3_out, nand_4_out, nand_5_out, nand_6_out, nand_7_out, nand_8_out, nand_9_out,
       nand_10_out, nand_11_out, nand_12_out, nand_13_out, nand_14_out, nand_15_out, nand_16_out,
       nand_17_out, nand_18_out, nand_19_out, nand_20_out, nand_21_out, nand_22_out, nand_23_out,
       nand_24_out, nand_25_out, nand_26_out, nand_27_out, nand_28_out, nand_29_out, nand_30_out,
       nand_31_out, nand_32_out, nand_33_out, nand_34_out, nand_35_out, nand_36_out, nand_37_out,
       nand_38_out, nand_39_out, nand_40_out, nand_41_out, nand_42_out, nand_43_out, nand_44_out,
       nand_45_out, nand_46_out, nand_47_out, nand_48_out, nand_49_out, nand_50_out, nand_51_out,
       nand_52_out, nand_53_out, nand_54_out, nand_55_out, nand_56_out, nand_57_out, nand_58_out;

  JKFlipFlop jkflipflop_1 (.SB(SB), .S(1'b1), .CLK(CLK), .R(1'b1), .O(O[0]));  // open: OC
  Mux2To1 mux2to1_1 (.A(O[0]), .B(I[0]), .S(L), .O(mux2to1_1_o));
  nand nand_1 (nand_1_out, mux2to1_1_o, mux2to1_1_o);
  Mux2To1 mux2to1_2 (.A(mux2to1_1_o), .B(nand_1_out), .S(L), .O(mux2to1_2_o));
  JKFlipFlop jkflipflop_2 (.SB(SB), .S(mux2to1_1_o), .CLK(CLK), .R(mux2to1_2_o), .O(O[1]));  // open: OC
  nand nand_2 (nand_2_out, O[0], O[1]);
  nand nand_3 (nand_3_out, nand_2_out, nand_2_out);
  Mux2To1 mux2to1_3 (.A(nand_3_out), .B(I[1]), .S(L), .O(mux2to1_3_o));
  nand nand_4 (nand_4_out, mux2to1_3_o, mux2to1_3_o);
  Mux2To1 mux2to1_4 (.A(mux2to1_3_o), .B(nand_4_out), .S(L), .O(mux2to1_4_o));
  JKFlipFlop jkflipflop_3 (.SB(SB), .S(mux2to1_3_o), .CLK(CLK), .R(mux2to1_4_o), .O(O[2]));  // open: OC
  nand nand_5 (nand_5_out, nand_3_out, O[2]);
  nand nand_6 (nand_6_out, nand_5_out, nand_5_out);
  Mux2To1 mux2to1_5 (.A(nand_6_out), .B(I[2]), .S(L), .O(mux2to1_5_o));
  nand nand_7 (nand_7_out, mux2to1_5_o, mux2to1_5_o);
  Mux2To1 mux2to1_6 (.A(mux2to1_5_o), .B(nand_7_out), .S(L), .O(mux2to1_6_o));
  JKFlipFlop jkflipflop_4 (.SB(SB), .S(mux2to1_5_o), .CLK(CLK), .R(mux2to1_6_o), .O(O[3]));  // open: OC
  nand nand_8 (nand_8_out, nand_6_out, O[3]);
  nand nand_9 (nand_9_out, nand_8_out, nand_8_out);
  Mux2To1 mux2to1_7 (.A(nand_9_out), .B(I[3]), .S(L), .O(mux2to1_7_o));
  nand nand_10 (nand_10_out, mux2to1_7_o, mux2to1_7_o);
  Mux2To1 mux2to1_8 (.A(mux2to1_7_o), .B(nand_10_out), .S(L), .O(mux2to1_8_o));
  JKFlipFlop jkflipflop_5 (.SB(SB), .S(mux2to1_7_o), .CLK(CLK), .R(mux2to1_8_o), .O(O[4]));  // open: OC
  nand nand_11 (nand_11_out, nand_9_out, O[4]);
  nand nand_12 (nand_12_out, nand_11_out, nand_11_out);
  Mux2To1 mux2to1_9 (.A(nand_12_out), .B(I[4]), .S(L), .O(mux2to1_9_o));
  nand nand_13 (nand_13_out, mux2to1_9_o, mux2to1_9_o);
  Mux2To1 mux2to1_10 (.A(mux2to1_9_o), .B(nand_13_out), .S(L), .O(mux2to1_10_o));
  JKFlipFlop jkflipflop_6 (.SB(SB), .S(mux2to1_9_o), .CLK(CLK), .R(mux2to1_10_o), .O(O[5]));  // open: OC
  nand nand_14 (nand_14_out, nand_12_out, O[5]);
  nand nand_15 (nand_15_out, nand_14_out, nand_14_out);
  Mux2To1 mux2to1_11 (.A(nand_15_out), .B(I[5]), .S(L), .O(mux2to1_11_o));
  nand nand_16 (nand_16_out, mux2to1_11_o, mux2to1_11_o);
  Mux2To1 mux2to1_12 (.A(mux2to1_11_o), .B(nand_16_out), .S(L), .O(mux2to1_12_o));
  JKFlipFlop jkflipflop_7 (.SB(SB), .S(mux2to1_11_o), .CLK(CLK), .R(mux2to1_12_o), .O(O[6]));  // open: OC
  nand nand_17 (nand_17_out, nand_15_out, O[6]);
  nand nand_18 (nand_18_out, nand_17_out, nand_17_out);
  Mux2To1 mux2to1_13 (.A(nand_18_out), .B(I[6]), .S(L), .O(mux2to1_13_o));
  nand nand_19 (nand_19_out, mux2to1_13_o, mux2to1_13_o);
  Mux2To1 mux2to1_14 (.A(mux2to1_13_o), .B(nand_19_out), .S(L), .O(mux2to1_14_o));
  JKFlipFlop jkflipflop_8 (.SB(SB), .S(mux2to1_13_o), .CLK(CLK), .R(mux2to1_14_o), .O(O[7]));  // open: OC
  nand nand_20 (nand_20_out, nand_18_out, O[7]);
  nand nand_21 (nand_21_out, nand_20_out, nand_20_out);
  Mux2To1 mux2to1_15 (.A(nand_21_out), .B(I[7]), .S(L), .O(mux2to1_15_o));
  nand nand_22 (nand_22_out, mux2to1_15_o, mux2to1_15_o);
  Mux2To1 mux2to1_16 (.A(mux2to1_15_o), .B(nand_22_out), .S(L), .O(mux2to1_16_o));
  JKFlipFlop jkflipflop_9 (.SB(SB), .S(mux2to1_15_o), .CLK(CLK), .R(mux2to1_16_o), .O(O[8]));  // open: OC
  nand nand_23 (nand_23_out, nand_21_out, O[8]);
  nand nand_24 (nand_24_out, nand_23_out, nand_23_out);
  Mux2To1 mux2to1_17 (.A(nand_24_out), .B(I[8]), .S(L), .O(mux2to1_17_o));
  nand nand_25 (nand_25_out, mux2to1_17_o, mux2to1_17_o);
  Mux2To1 mux2to1_18 (.A(mux2to1_17_o), .B(nand_25_out), .S(L), .O(mux2to1_18_o));
  JKFlipFlop jkflipflop_10 (.SB(SB), .S(mux2to1_17_o), .CLK(CLK), .R(mux2to1_18_o), .O(O[9]));  // open: OC
  nand nand_26 (nand_26_out, nand_24_out, O[9]);
  nand nand_27 (nand_27_out, nand_26_out, nand_26_out);
  Mux2To1 mux2to1_19 (.A(nand_27_out), .B(I[9]), .S(L), .O(mux2to1_19_o));
  nand nand_28 (nand_28_out, mux2to1_19_o, mux2to1_19_o);
  Mux2To1 mux2to1_20 (.A(mux2to1_19_o), .B(nand_28_out), .S(L), .O(mux2to1_20_o));
  JKFlipFlop jkflipflop_11 (.SB(SB), .S(mux2to1_19_o), .CLK(CLK), .R(mux2to1_20_o), .O(O[10]));  // open: OC
  nand nand_29 (nand_29_out, nand_27_out, O[10]);
  nand nand_30 (nand_30_out, nand_29_out, nand_29_out);
  Mux2To1 mux2to1_21 (.A(nand_30_out), .B(I[10]), .S(L), .O(mux2to1_21_o));
  nand nand_31 (nand_31_out, mux2to1_21_o, mux2to1_21_o);
  Mux2To1 mux2to1_22 (.A(mux2to1_21_o), .B(nand_31_out), .S(L), .O(mux2to1_22_o));
  JKFlipFlop jkflipflop_12 (.SB(SB), .S(mux2to1_21_o), .CLK(CLK), .R(mux2to1_22_o), .O(jkflipflop_12_o));  // open: OC
  nand nand_32 (nand_32_out, nand_30_out, jkflipflop_12_o);
  nand nand_33 (nand_33_out, nand_32_out, nand_32_out);
  Mux2To1 mux2to1_23 (.A(nand_33_out), .B(I[11]), .S(L), .O(mux2to1_23_o));
  nand nand_34 (nand_34_out, mux2to1_23_o, mux2to1_23_o);
  Mux2To1 mux2to1_24 (.A(mux2to1_23_o), .B(nand_34_out), .S(L), .O(mux2to1_24_o));
  JKFlipFlop jkflipflop_13 (.SB(SB), .S(mux2to1_23_o), .CLK(CLK), .R(mux2to1_24_o), .O(O[11]));  // open: OC
  nand nand_35 (nand_35_out, nand_33_out, O[11]);
  nand nand_36 (nand_36_out, nand_35_out, nand_35_out);
  Mux2To1 mux2to1_25 (.A(nand_36_out), .B(I[12]), .S(L), .O(mux2to1_25_o));
  nand nand_37 (nand_37_out, mux2to1_25_o, mux2to1_25_o);
  Mux2To1 mux2to1_26 (.A(mux2to1_25_o), .B(nand_37_out), .S(L), .O(mux2to1_26_o));
  JKFlipFlop jkflipflop_14 (.SB(SB), .S(mux2to1_25_o), .CLK(CLK), .R(mux2to1_26_o), .O(O[12]));  // open: OC
  nand nand_38 (nand_38_out, nand_36_out, O[12]);
  nand nand_39 (nand_39_out, nand_38_out, nand_38_out);
  Mux2To1 mux2to1_27 (.A(nand_39_out), .B(I[13]), .S(L), .O(mux2to1_27_o));
  nand nand_40 (nand_40_out, mux2to1_27_o, mux2to1_27_o);
  Mux2To1 mux2to1_28 (.A(mux2to1_27_o), .B(nand_40_out), .S(L), .O(mux2to1_28_o));
  JKFlipFlop jkflipflop_15 (.SB(SB), .S(mux2to1_27_o), .CLK(CLK), .R(mux2to1_28_o), .O(O[13]));  // open: OC
  nand nand_41 (nand_41_out, nand_39_out, O[13]);
  nand nand_42 (nand_42_out, nand_41_out, nand_41_out);
  Mux2To1 mux2to1_29 (.A(nand_42_out), .B(I[14]), .S(L), .O(mux2to1_29_o));
  nand nand_43 (nand_43_out, mux2to1_29_o, mux2to1_29_o);
  Mux2To1 mux2to1_30 (.A(mux2to1_29_o), .B(nand_43_out), .S(L), .O(mux2to1_30_o));
  JKFlipFlop jkflipflop_16 (.SB(SB), .S(mux2to1_29_o), .CLK(CLK), .R(mux2to1_30_o), .O(O[14]));  // open: OC
  nand nand_44 (nand_44_out, nand_42_out, O[14]);
  nand nand_45 (nand_45_out, nand_44_out, nand_44_out);
  Mux2To1 mux2to1_31 (.A(nand_45_out), .B(I[15]), .S(L), .O(mux2to1_31_o));
  nand nand_46 (nand_46_out, mux2to1_31_o, mux2to1_31_o);
  Mux2To1 mux2to1_32 (.A(mux2to1_31_o), .B(nand_46_out), .S(L), .O(mux2to1_32_o));
  JKFlipFlop jkflipflop_17 (.SB(SB), .S(mux2to1_31_o), .CLK(CLK), .R(mux2to1_32_o), .O(O[15]));  // open: OC
  nand nand_47 (nand_47_out, nand_45_out, O[15]);
  nand nand_48 (nand_48_out, nand_47_out, nand_47_out);
  Mux2To1 mux2to1_33 (.A(nand_48_out), .B(I[16]), .S(L), .O(mux2to1_33_o));
  nand nand_49 (nand_49_out, mux2to1_33_o, mux2to1_33_o);
  Mux2To1 mux2to1_34 (.A(mux2to1_33_o), .B(nand_49_out), .S(L), .O(mux2to1_34_o));
  JKFlipFlop jkflipflop_18 (.SB(SB), .S(mux2to1_33_o), .CLK(CLK), .R(mux2to1_34_o), .O(O[16]));  // open: OC
  nand nand_50 (nand_50_out, nand_48_out, O[16]);
  nand nand_51 (nand_51_out, nand_50_out, nand_50_out);
  Mux2To1 mux2to1_35 (.A(nand_51_out), .B(I[17]), .S(L), .O(mux2to1_35_o));
  nand nand_52 (nand_52_out, mux2to1_35_o, mux2to1_35_o);
  Mux2To1 mux2to1_36 (.A(mux2to1_35_o), .B(nand_52_out), .S(L), .O(mux2to1_36_o));
  JKFlipFlop jkflipflop_19 (.SB(SB), .S(mux2to1_35_o), .CLK(CLK), .R(mux2to1_36_o), .O(O[17]));  // open: OC
  nand nand_53 (nand_53_out, nand_51_out, O[17]);
  nand nand_54 (nand_54_out, nand_53_out, nand_53_out);
  Mux2To1 mux2to1_37 (.A(nand_54_out), .B(I[18]), .S(L), .O(mux2to1_37_o));
  nand nand_55 (nand_55_out, mux2to1_37_o, mux2to1_37_o);
  Mux2To1 mux2to1_38 (.A(mux2to1_37_o), .B(nand_55_out), .S(L), .O(mux2to1_38_o));
  JKFlipFlop jkflipflop_20 (.SB(SB), .S(mux2to1_37_o), .CLK(CLK), .R(mux2to1_38_o), .O(O[18]));  // open: OC
  nand nand_56 (nand_56_out, nand_54_out, O[18]);
  nand nand_57 (nand_57_out, nand_56_out, nand_56_out);
  Mux2To1 mux2to1_39 (.A(nand_57_out), .B(I[19]), .S(L), .O(mux2to1_39_o));
  nand nand_58 (nand_58_out, mux2to1_39_o, mux2to1_39_o);
  Mux2To1 mux2to1_40 (.A(mux2to1_39_o), .B(nand_58_out), .S(L), .O(mux2to1_40_o));
  JKFlipFlop jkflipflop_21 (.SB(SB), .S(mux2to1_39_o), .CLK(CLK), .R(mux2to1_40_o), .O(O[19]));  // open: OC
endmodule

module JKFlipFlop (
  input  SB,
  input  S,
  input  CLK,
  input  R,
  output O,
  output OC
);

  wire nand_1_out, nand_2_out, nand_3_out, nand_4_out, nand_5_out, nand_6_out, nand_7_out, nand_8_out,
       nand_9_out, nand_10_out, nand_11_out;

  nand nand_1 (nand_1_out, OC, S);
  nand nand_2 (nand_2_out, R, O);
  nand nand_3 (nand_3_out, nand_1_out, nand_1_out);
  nand nand_4 (nand_4_out, nand_2_out, nand_2_out);
  nand nand_5 (nand_5_out, nand_3_out, CLK);
  nand nand_6 (nand_6_out, CLK, nand_4_out);
  nand nand_7 (nand_7_out, nand_5_out, SB, nand_8_out);
  nand nand_8 (nand_8_out, nand_7_out, nand_6_out);
  nand nand_9 (nand_9_out, CLK, CLK);
  nand nand_10 (nand_10_out, nand_7_out, nand_9_out);
  nand nand_11 (nand_11_out, nand_9_out, nand_8_out);
  nand nand_12 (O, nand_10_out, SB, OC);
  nand nand_13 (OC, O, nand_11_out);
endmodule

module ALU (
  input  [9:0] A,
  input  [9:0] B,
  input  AZ,
  input  AC,
  input  BZ,
  input  BC,
  input  Cin,
  input  N,
  input  OC,
  output Cout,
  output [9:0] O
);

  wire [9:0] fulladder10_1_o, inverter10_1_o, inverter10_2_o, inverter10_3_o, mux2to1_10_1_o, mux2to1_10_2_o,
       mux2to1_10_3_o, mux2to1_10_4_o, mux2to1_10_5_o, nand10_1_o;

  Mux2To1_10 mux2to1_10_1 (.A(A), .B({10{1'b0}}), .S(AZ), .O(mux2to1_10_1_o));
  Mux2To1_10 mux2to1_10_2 (.A(B), .B({10{1'b0}}), .S(BZ), .O(mux2to1_10_2_o));
  Inverter10 inverter10_1 (.I(mux2to1_10_1_o), .O(inverter10_1_o));
  Inverter10 inverter10_2 (.I(mux2to1_10_2_o), .O(inverter10_2_o));
  Mux2To1_10 mux2to1_10_3 (.A(mux2to1_10_1_o), .B(inverter10_1_o), .S(AC), .O(mux2to1_10_3_o));
  Mux2To1_10 mux2to1_10_4 (.A(mux2to1_10_2_o), .B(inverter10_2_o), .S(BC), .O(mux2to1_10_4_o));
  FullAdder10 fulladder10_1 (.Cin(Cin), .A(mux2to1_10_3_o), .B(mux2to1_10_4_o), .O(fulladder10_1_o), .Cout(Cout));
  Nand10 nand10_1 (.A(mux2to1_10_3_o), .B(mux2to1_10_4_o), .O(nand10_1_o));
  Mux2To1_10 mux2to1_10_5 (.A(fulladder10_1_o), .B(nand10_1_o), .S(N), .O(mux2to1_10_5_o));
  Inverter10 inverter10_3 (.I(mux2to1_10_5_o), .O(inverter10_3_o));
  Mux2To1_10 mux2to1_10_6 (.A(mux2to1_10_5_o), .B(inverter10_3_o), .S(OC), .O(O));
endmodule

module Mux2To1_10 (
  input  [9:0] A,
  input  [9:0] B,
  input  S,
  output [9:0] O
);

  Mux2To1 mux2to1_1 (.A(A[0]), .B(B[0]), .S(S), .O(O[0]));
  Mux2To1 mux2to1_2 (.A(A[1]), .B(B[1]), .S(S), .O(O[1]));
  Mux2To1 mux2to1_3 (.A(A[2]), .B(B[2]), .S(S), .O(O[2]));
  Mux2To1 mux2to1_4 (.A(A[3]), .B(B[3]), .S(S), .O(O[3]));
  Mux2To1 mux2to1_5 (.A(A[4]), .B(B[4]), .S(S), .O(O[4]));
  Mux2To1 mux2to1_6 (.A(A[5]), .B(B[5]), .S(S), .O(O[5]));
  Mux2To1 mux2to1_7 (.A(A[6]), .B(B[6]), .S(S), .O(O[6]));
  Mux2To1 mux2to1_8 (.A(A[7]), .B(B[7]), .S(S), .O(O[7]));
  Mux2To1 mux2to1_9 (.A(A[8]), .B(B[8]), .S(S), .O(O[8]));
  Mux2To1 mux2to1_10 (.A(A[9]), .B(B[9]), .S(S), .O(O[9]));
endmodule

module Inverter10 (
  input  [9:0] I,
  output [9:0] O
);

  Nand10 nand10_1 (.A(I), .B(I), .O(O));
endmodule

module FullAdder (
  input  A,
  input  B,
  input  Cin,
  output O,
  output Cout
);

  wire nand_1_out, nand_2_out, nand_3_out, nand_4_out, nand_5_out, nand_6_out, nand_7_out, nand_8_out,
       nand_9_out, nand_10_out, nand_11_out;

  nand nand_1 (nand_1_out, A, A);
  nand nand_2 (nand_2_out, B, B);
  nand nand_3 (nand_3_out, B, A);
  nand nand_4 (nand_4_out, A, nand_2_out);
  nand nand_5 (nand_5_out, nand_1_out, B);
  nand nand_6 (nand_6_out, nand_4_out, nand_5_out);
  nand nand_7 (nand_7_out, nand_6_out, nand_6_out);
  nand nand_8 (nand_8_out, Cin, Cin);
  nand nand_9 (nand_9_out, Cin, nand_6_out);
  nand nand_10 (nand_10_out, nand_6_out, nand_8_out);
  nand nand_11 (nand_11_out, nand_7_out, Cin);
  nand nand_12 (O, nand_10_out, nand_11_out);
  nand nand_13 (Cout, nand_9_out, nand_3_out);
endmodule

module HalfAdder (
  input  A,
  input  B,
  output S,
  output C
);

  wire nand_1_out, nand_2_out, nand_3_out, nand_5_out, nand_6_out;

  nand nand_1 (nand_1_out, A, A);
  nand nand_2 (nand_2_out, B, B);
  nand nand_3 (nand_3_out, B, A);
  nand nand_4 (C, nand_3_out, nand_3_out);
  nand nand_5 (nand_5_out, A, nand_2_out);
  nand nand_6 (nand_6_out, nand_1_out, B);
  nand nand_7 (S, nand_5_out, nand_6_out);
endmodule

module FullAdder10 (
  input  Cin,
  input  [9:0] A,
  input  [9:0] B,
  output [9:0] O,
  output Cout
);

  wire fulladder_1_cout, fulladder_2_cout, fulladder_3_cout, fulladder_4_cout, fulladder_5_cout,
       fulladder_6_cout, fulladder_7_cout, fulladder_8_cout, fulladder_9_cout;

  FullAdder fulladder_1 (.A(A[0]), .B(B[0]), .Cin(Cin), .O(O[0]), .Cout(fulladder_1_cout));
  FullAdder fulladder_2 (.A(A[1]), .B(B[1]), .Cin(fulladder_1_cout), .O(O[1]), .Cout(fulladder_2_cout));
  FullAdder fulladder_3 (.A(A[2]), .B(B[2]), .Cin(fulladder_2_cout), .O(O[2]), .Cout(fulladder_3_cout));
  FullAdder fulladder_4 (.A(A[3]), .B(B[3]), .Cin(fulladder_3_cout), .O(O[3]), .Cout(fulladder_4_cout));
  FullAdder fulladder_5 (.A(A[4]), .B(B[4]), .Cin(fulladder_4_cout), .O(O[4]), .Cout(fulladder_5_cout));
  FullAdder fulladder_6 (.A(A[5]), .B(B[5]), .Cin(fulladder_5_cout), .O(O[5]), .Cout(fulladder_6_cout));
  FullAdder fulladder_7 (.A(A[6]), .B(B[6]), .Cin(fulladder_6_cout), .O(O[6]), .Cout(fulladder_7_cout));
  FullAdder fulladder_8 (.A(A[7]), .B(B[7]), .Cin(fulladder_7_cout), .O(O[7]), .Cout(fulladder_8_cout));
  FullAdder fulladder_9 (.A(A[8]), .B(B[8]), .Cin(fulladder_8_cout), .O(O[8]), .Cout(fulladder_9_cout));
  FullAdder fulladder_10 (.A(A[9]), .B(B[9]), .Cin(fulladder_9_cout), .O(O[9]), .Cout(Cout));
endmodule

module Nand10 (
  input  [9:0] A,
  input  [9:0] B,
  output [9:0] O
);

  nand nand_1 (O[0], A[0], B[0]);
  nand nand_2 (O[1], A[1], B[1]);
  nand nand_3 (O[2], A[2], B[2]);
  nand nand_4 (O[3], A[3], B[3]);
  nand nand_5 (O[4], A[4], B[4]);
  nand nand_6 (O[5], A[5], B[5]);
  nand nand_7 (O[6], A[6], B[6]);
  nand nand_8 (O[7], A[7], B[7]);
  nand nand_9 (O[8], A[8], B[8]);
  nand nand_10 (O[9], A[9], B[9]);
endmodule

module Buffer10 (
  input  [9:0] I,
  input  E,
  output [9:0] O
);

  assign O[0] = E ? I[0] : 1'bz;  // Controlled_Buffer controlled_buffer_1
  assign O[1] = E ? I[1] : 1'bz;  // Controlled_Buffer controlled_buffer_2
  assign O[2] = E ? I[2] : 1'bz;  // Controlled_Buffer controlled_buffer_3
  assign O[3] = E ? I[3] : 1'bz;  // Controlled_Buffer controlled_buffer_4
  assign O[4] = E ? I[4] : 1'bz;  // Controlled_Buffer controlled_buffer_5
  assign O[5] = E ? I[5] : 1'bz;  // Controlled_Buffer controlled_buffer_6
  assign O[6] = E ? I[6] : 1'bz;  // Controlled_Buffer controlled_buffer_7
  assign O[7] = E ? I[7] : 1'bz;  // Controlled_Buffer controlled_buffer_8
  assign O[8] = E ? I[8] : 1'bz;  // Controlled_Buffer controlled_buffer_9
  assign O[9] = E ? I[9] : 1'bz;  // Controlled_Buffer controlled_buffer_10
endmodule

module ALUFlagsRegister (
  input  CLK,
  input  LL,
  input  LH,
  input  SB,
  input  [6:0] I,
  output [6:0] O
);

  wire nand_1_out, nand_2_out, nand_3_out, nand_4_out;

  nand nand_1 (nand_1_out, CLK, LL);
  nand nand_2 (nand_2_out, nand_1_out, nand_1_out);
  nand nand_3 (nand_3_out, CLK, LH);
  nand nand_4 (nand_4_out, nand_3_out, nand_3_out);
  DLatch dlatch_1 (.E(nand_2_out), .D(I[0]), .SB(SB), .O(O[0]));  // open: OC
  DLatch dlatch_2 (.E(nand_2_out), .D(I[1]), .SB(SB), .O(O[1]));  // open: OC
  DLatch dlatch_3 (.E(nand_2_out), .D(I[2]), .SB(SB), .O(O[2]));  // open: OC
  DLatch dlatch_4 (.E(nand_2_out), .D(I[3]), .SB(SB), .O(O[3]));  // open: OC
  DLatch dlatch_5 (.E(nand_2_out), .D(I[4]), .SB(SB), .O(O[4]));  // open: OC
  DLatch dlatch_6 (.E(nand_4_out), .D(I[5]), .SB(SB), .O(O[5]));  // open: OC
  DLatch dlatch_7 (.E(nand_4_out), .D(I[6]), .SB(SB), .O(O[6]));  // open: OC
endmodule

module Mux2To1_20 (
  input  [19:0] A,
  input  [19:0] B,
  input  S,
  output [19:0] O
);

  Mux2To1_10 mux2to1_10_1 (.A(A[9:0]), .B(B[9:0]), .S(S), .O(O[9:0]));
  Mux2To1_10 mux2to1_10_2 (.A(A[19:10]), .B(B[19:10]), .S(S), .O(O[19:10]));
endmodule
